# Fritzing sketch ufo wiring sketch (saved by Fritzing 0.9.2b)

parts:
  Adafruit_HUZZAH_ESP8266_Breakout1 = Adafruit HUZZAH ESP8266 Breakout [part_number=2471]
  NEOPIXEL1 = Neopixel Strip -- Black (30/m)
  NEOPIXEL2 = Neopixel Strip -- Black (30/m)
  NEOPIXEL3 = Neopixel Strip -- Black (30/m)
  NEOPIXEL4 = Neopixel Strip -- Black (30/m)
  S4 = Momentary Switch [package=ksa_sealed_tac_switch]
  CONN1 = USB connector [package=THT]
  J1 = female pin header, 1 pin [form="♀ (female)"]
  J2 = female pin header, 1 pin [form="♀ (female)"]
  J3 = male pin header, 5 pins [form="♂ (male)"]

nets:
  GND: Adafruit_HUZZAH_ESP8266_Breakout1.GND, NEOPIXEL1.GND, NEOPIXEL2.GND, NEOPIXEL3.GND#1, CONN1.GND, CONN1.chassis5, CONN1.chassis6, J2.pin1, J3.pin5
  +5V: Adafruit_HUZZAH_ESP8266_Breakout1.VBat, NEOPIXEL1.+5V, NEOPIXEL2.+5V, NEOPIXEL3.+5V#3, CONN1.d-, J1.pin1
  N1: Adafruit_HUZZAH_ESP8266_Breakout1.#5, NEOPIXEL2.Din
  N2: Adafruit_HUZZAH_ESP8266_Breakout1.#4, NEOPIXEL1.Din
  N3: Adafruit_HUZZAH_ESP8266_Breakout1.#2, NEOPIXEL3.Din
  N4: Adafruit_HUZZAH_ESP8266_Breakout1.#15, S4.2
  N5: Adafruit_HUZZAH_ESP8266_Breakout1.3V, S4.1
  N6: Adafruit_HUZZAH_ESP8266_Breakout1.V+, J3.pin3
  N7: Adafruit_HUZZAH_ESP8266_Breakout1.RX, J3.pin2
  N8: Adafruit_HUZZAH_ESP8266_Breakout1.TX, J3.pin1
  N9: NEOPIXEL3.+5V#4, NEOPIXEL4.+5V
  N10: NEOPIXEL3.Dout, NEOPIXEL4.Din
  N11: NEOPIXEL3.GND#6, NEOPIXEL4.GND

notes:
  strip 30 leds - upper ring
  strip 30 leds - lower ring
  2 strips 2 leds each - downlight
  wifi reset button
  2000mA 5V power supply
  FTDI connector
  Dynatrace UFO

custom parts:
  Neopixel Strip -- Black (30/m): These NeoPixel strips have 30 digitally-addressable pixel LEDs per meter and are very affordable and are only 12.5 mm wide, 10 mm if you remove the strip from the casing.
